// Logisim project control.circ as structural Verilog: 3 circuits, main circuit ALUcontrol_0
module ALUcontrol_0 (
  input  ALUop_1,
  input  ALUop_0,
  input  F5,
  input  F4,
  input  F3,
  input  F2,
  input  F1,
  input  F0,
  output Operation_3,
  output Operation_2,
  output Operation_1,
  output Operation_0
);

  wire and_2_out, and_3_out, and_4_out, not_1_out, not_2_out, not_3_out;

  and and_1 (Operation_3, ALUop_1, F1, F0);
  and and_2 (and_2_out, F1, ALUop_1);
  not not_1 (not_1_out, F2);
  or or_1 (Operation_1, not_1_out, not_2_out);
  not not_2 (not_2_out, ALUop_1);
  and and_3 (and_3_out, F3, ALUop_1);
  and and_4 (and_4_out, F0, not_3_out, ALUop_1);
  not not_3 (not_3_out, F1);
  or or_2 (Operation_2, ALUop_0, and_2_out);
  or or_3 (Operation_0, and_3_out, and_4_out);
endmodule

module Control_0 (
  input  op_5,
  input  op_4,
  input  op_3,
  input  op_2,
  input  op_1,
  input  op_0,
  output RegDst,
  output Branch,
  output MemRead,
  output MemToReg,
  output MemWrite,
  output ALUsrc,
  output RegWrite
);

  wire and_5_out, and_6_out, not_1_out, not_2_out, not_3_out, not_4_out, not_5_out, not_6_out, not_7_out;

  not not_1 (not_1_out, op_3);
  not not_2 (not_2_out, op_1);
  not not_3 (not_3_out, op_3);
  not not_4 (not_4_out, op_3);
  and and_1 (MemWrite, op_5, op_3);
  or or_1 (ALUsrc, op_1, op_3);
  not not_5 (not_5_out, op_2);
  not not_6 (not_6_out, op_0);
  not not_7 (not_7_out, op_3);
  and and_2 (RegDst, not_1_out, not_2_out);
  and and_3 (MemRead, not_3_out, op_1);
  and and_4 (MemToReg, not_4_out, op_1);
  and and_5 (and_5_out, not_5_out, not_6_out);
  and and_6 (and_6_out, not_7_out, op_1);
  or or_2 (RegWrite, and_5_out, and_6_out);

  assign Branch = op_2;
endmodule

module Control_1 (
  input  op_5,
  input  op_4,
  input  op_3,
  input  op_2,
  input  op_1,
  input  op_0,
  output ALUop_1,
  output ALUop_0
);

  wire and_1_out, and_2_out, and_3_out, not_1_out, not_2_out, not_3_out, not_4_out, not_5_out;

  not not_1 (not_1_out, op_3);
  not not_2 (not_2_out, op_2);
  not not_3 (not_3_out, op_0);
  not not_4 (not_4_out, op_5);
  not not_5 (not_5_out, op_5);
  and and_1 (and_1_out, not_1_out, not_2_out, not_3_out);
  and and_2 (and_2_out, not_4_out, op_1);
  and and_3 (and_3_out, not_5_out, op_1);
  or or_1 (ALUop_1, and_1_out, and_2_out);
  or or_2 (ALUop_0, and_3_out, op_2);
endmodule
