// Logisim project pipelineComponentsBrancing.circ as structural Verilog: 3 circuits, main circuit Datapath
module Datapath (
  input  Reset,
  input  Clear,
  input  Clear_2
);

  wire alucontrol_1_p3, and_1_out, and_3_out, and_4_out, control_1_p2, instructiondecode_1_p2,
       instructiondecode_1_p3, instructiondecode_1_p7, not_1_out, not_2_out, not_3_out, signextend_1_p3;
  wire [0:0] alu_1_p4;
  wire [1:0] control_1_p6, register_16_q;
  wire [4:0] instructiondecode_1_p4, instructiondecode_1_p5, multiplexer_2_out, register_8_q, register_15_q,
       registers_1_p2;
  wire [5:0] instructiondecode_1_p6, register_10_q, register_12_q;
  wire [7:0] control_1_p3, register_5_q, wordaddress_1_p2, wordaddress_2_p2;
  wire [31:0] adder_1_out, alu_1_p5, branchaddress_1_p3, control_1_p10, memorydata_1_p3, memorydata_1_p6,
       multiplexer_1_out, multiplexer_3_out, ram_1_data, register_1_q, register_2_q, register_3_q,
       register_4_q, register_6_q, register_7_q, register_9_q, register_11_q, register_13_q, register_14_q,
       register_17_q, register_18_q, registers_1_p11, registers_1_p12, signextend_1_p2;

  Register #(.width(32)) register_1 (
    .D(multiplexer_1_out), .Q(register_1_q), .clk(signextend_1_p3), .clr(Reset));  // open: en
  Multiplexer #(.width(32), .enable("false")) multiplexer_1 (
    .in0(adder_1_out), .in1(register_11_q), .out(multiplexer_1_out), .sel(and_3_out));
  // WordAddress wordaddress_1: pin names not known; wires that end beside it: register_1_q, wordaddress_1_p2
  Register #(.width(32)) register_2 (
    .D(adder_1_out), .Q(register_2_q), .clk(signextend_1_p3), .clr(Reset));  // open: en
  Adder #(.width(32)) adder_1 (.a(32'h4), .b(register_1_q), .out(adder_1_out));  // open: cin, cout
  Register #(.width(32)) register_3 (.D(ram_1_data), .Q(register_3_q), .clk(signextend_1_p3), .clr(Reset));  // open: en
  // InstructionDecode instructiondecode_1: pin names not known; wires that end beside it: register_3_q, instructiondecode_1_p2, instructiondecode_1_p3, instructiondecode_1_p4, instructiondecode_1_p5, instructiondecode_1_p6, instructiondecode_1_p7
  RAM #(.dataWidth(32)) ram_1 (
    .addr(wordaddress_1_p2), .data(ram_1_data), .sel(1'b1), .clk(1'b0), .ld(1'b1), .clr(Clear));
  // Control control_1: pin names not known; wires that end beside it: instructiondecode_1_p2, control_1_p2, control_1_p3[0], control_1_p3[1], control_1_p3[2], control_1_p6, control_1_p3[5], control_1_p3[6], control_1_p3[7], control_1_p10
  Multiplexer #(.width(5), .enable("false")) multiplexer_2 (
    .in0(instructiondecode_1_p4), .in1(instructiondecode_1_p5), .out(multiplexer_2_out), .sel(control_1_p2));
  not not_1 (not_1_out, signextend_1_p3);
  // SignExtend signextend_1: pin names not known; wires that end beside it: instructiondecode_1_p7, signextend_1_p2, signextend_1_p3
  and and_1 (and_1_out, not_1_out, register_16_q[1]);
  // RegisterFile registerfile_1: pin names not known
  // Registers registers_1: pin names not known; wires that end beside it: register_16_q[1], registers_1_p2, instructiondecode_1_p3, instructiondecode_1_p4, instructiondecode_1_p3, instructiondecode_1_p4, registers_1_p2, control_1_p10, and_1_out, Reset, registers_1_p11, registers_1_p12
  Register #(.width(32)) register_4 (
    .D(register_2_q), .Q(register_4_q), .clk(signextend_1_p3), .clr(Reset));  // open: en
  Register register_5 (
    .D({control_1_p3[7:5], control_1_p6, control_1_p3[2:0]}), .Q(register_5_q), .clk(signextend_1_p3),
    .clr(Reset));  // open: en
  Register #(.width(32)) register_6 (
    .D(registers_1_p11), .Q(register_6_q), .clk(signextend_1_p3), .clr(Reset));  // open: en
  Register #(.width(32)) register_7 (
    .D(registers_1_p12), .Q(register_7_q), .clk(signextend_1_p3), .clr(Reset));  // open: en
  Register #(.width(5)) register_8 (
    .D(multiplexer_2_out), .Q(register_8_q), .clk(signextend_1_p3), .clr(Reset));  // open: en
  Register #(.width(32)) register_9 (
    .D(signextend_1_p2), .Q(register_9_q), .clk(signextend_1_p3), .clr(Reset));  // open: en
  Register #(.width(6)) register_10 (
    .D(instructiondecode_1_p6), .Q(register_10_q), .clk(signextend_1_p3), .clr(Reset));  // open: en
  // BranchAddress branchaddress_1: pin names not known; wires that end beside it: register_4_q, register_9_q, branchaddress_1_p3
  Multiplexer #(.width(32), .enable("false")) multiplexer_3 (
    .in0(register_7_q), .in1(register_9_q), .out(multiplexer_3_out), .sel(register_5_q[6]));
  // ALUcontrol alucontrol_1: pin names not known; wires that end beside it: register_10_q, register_5_q[4:3], alucontrol_1_p3
  // ALU alu_1: pin names not known; wires that end beside it: register_6_q, multiplexer_3_out, alucontrol_1_p3, alu_1_p4[0], alu_1_p5
  // AND_Gate and_2 is placed but not wired
  Register #(.width(32)) register_11 (
    .D(branchaddress_1_p3), .Q(register_11_q), .clk(signextend_1_p3), .clr(Reset));  // open: en
  Register #(.width(6)) register_12 (
    .D({register_5_q[7], register_5_q[5], register_5_q[2:0], alu_1_p4[0]}), .Q(register_12_q),
    .clk(signextend_1_p3), .clr(Reset));  // open: en
  Register #(.width(32)) register_13 (.D(alu_1_p5), .Q(register_13_q), .clk(signextend_1_p3), .clr(Reset));  // open: en
  Register #(.width(32)) register_14 (
    .D(register_7_q), .Q(register_14_q), .clk(signextend_1_p3), .clr(Reset));  // open: en
  Register #(.width(5)) register_15 (
    .D(register_8_q), .Q(register_15_q), .clk(signextend_1_p3), .clr(Reset));  // open: en
  // MemoryData memorydata_1: pin names not known; wires that end beside it: register_12_q[5], register_14_q, memorydata_1_p3, register_12_q[4], register_12_q[2], memorydata_1_p6, memorydata_1_p3
  and and_3 (and_3_out, register_12_q[0], register_12_q[1]);
  // WordAddress wordaddress_2: pin names not known; wires that end beside it: register_13_q, wordaddress_2_p2
  not not_2 (not_2_out, signextend_1_p3);
  Register #(.width(2)) register_16 (
    .D({register_12_q[5], register_12_q[3]}), .Q(register_16_q), .clk(signextend_1_p3), .clr(Reset));  // open: en
  Register #(.width(32)) register_17 (
    .D(register_13_q), .Q(register_17_q), .clk(signextend_1_p3), .clr(Reset));  // open: en
  Register #(.width(32)) register_18 (
    .D(memorydata_1_p6), .Q(register_18_q), .clk(signextend_1_p3), .clr(Reset));  // open: en
  Register #(.width(5)) register_19 (
    .D(register_15_q), .Q(registers_1_p2), .clk(signextend_1_p3), .clr(Reset));  // open: en
  Clock Clock (.out(signextend_1_p3));
  and and_4 (and_4_out, not_2_out, register_12_q[4]);
  RAM #(.dataWidth(32)) ram_2 (
    .addr(wordaddress_2_p2), .data(memorydata_1_p3), .sel(1'b1), .clk(and_4_out), .ld(register_12_q[2]),
    .clr(Clear_2));
  Multiplexer #(.width(32), .enable("false")) multiplexer_4 (
    .in0(register_17_q), .in1(register_18_q), .out(control_1_p10), .sel(register_16_q[0]));
  not not_3 (not_3_out, 1'b0);
  Counter #(.ongoal("continue")) counter_1 (
    .load(1'b0), .count(not_3_out), .clk(signextend_1_p3));  // open: D, Q, carry, clr

  // Notes on the sheet:
  //   Today's Date
  //   Your Name
  //   PC
  //   IF/ID
  //   Instruction Memory
  //   Decode
  //   IF/ID.rs
  //   IF/ID.rt
  //   IF/ID.rd
  //   Control
  //   Extend
  //   ID/EX
  //   Branch
  //   ALU
  //   ALU control
  //   EX/MEM
  //   regwrite
  //   MEM/WB
  //   Data Memory
endmodule

module Equality (
  input  [31:0] in_1,
  input  [31:0] in_2,
  output _0
);

  wire [31:0] xor_1_out;

  assign xor_1_out = in_1 ^ in_2;  // XOR_Gate xor_1, 32 bits wide
  // Zero zero_1: pin names not known; wires that end beside it: xor_1_out, _0
endmodule

module brancheq (
  input  [4:0] in_1,
  input  [4:0] in_2,
  output _0
);

  wire [31:0] zero_1_p1;

  // Zero zero_1: pin names not known; wires that end beside it: zero_1_p1, _0
  assign zero_1_p1 = {{27{1'b0}}, in_1} ^ {{27{1'b0}}, in_2};  // XOR_Gate xor_1, 32 bits wide
endmodule
