// Logisim project pipelineComponentsBrancingv4.circ as structural Verilog: 3 circuits, main circuit Datapath
module Datapath (
  input  Reset,
  input  Clear,
  input  Clear_2
);

  wire alucontrol_1_p3, and_1_out, and_2_out, and_4_out, branchaddress_2_p3, brancheq_1_out_6, control_1_p2,
       instructiondecode_1_p2, instructiondecode_1_p7, not_1_out, not_2_out, not_3_out, registerfile_1_p2;
  wire [0:0] alu_1_p4;
  wire [1:0] control_1_p6, register_16_q;
  wire [4:0] instructiondecode_1_p3, instructiondecode_1_p4, instructiondecode_1_p5, multiplexer_2_out,
       register_8_q, register_15_q, registerfile_1_p4;
  wire [5:0] instructiondecode_1_p6, register_10_q, register_12_q;
  wire [7:0] control_1_p3, register_5_q, wordaddress_1_p2, wordaddress_2_p2;
  wire [31:0] adder_1_out, alu_1_p5, branchaddress_1_p1, branchaddress_1_p2, branchaddress_1_p3,
       branchaddress_2_p4, branchaddress_2_p5, memorydata_1_p3, memorydata_1_p6, multiplexer_1_out,
       multiplexer_3_out, ram_1_data, register_1_q, register_3_q, register_4_q, register_6_q, register_7_q,
       register_9_q, register_13_q, register_14_q, register_17_q, register_18_q, registerfile_1_p1,
       registers_1_p7, registers_1_p8;

  Multiplexer #(.width(32), .enable("false")) multiplexer_1 (
    .in0(adder_1_out), .in1(branchaddress_1_p1), .out(multiplexer_1_out), .sel(and_1_out));
  Register #(.width(32)) register_1 (
    .D(multiplexer_1_out), .Q(register_1_q), .clk(registerfile_1_p2), .clr(Reset));  // open: en
  // WordAddress wordaddress_1: pin names not known; wires that end beside it: register_1_q, wordaddress_1_p2
  // BranchAddress branchaddress_1: pin names not known; wires that end beside it: branchaddress_1_p1, branchaddress_1_p2, branchaddress_1_p3
  Adder #(.width(32)) adder_1 (.a(32'h4), .b(register_1_q), .out(adder_1_out));  // open: cin, cout
  Register #(.width(32)) register_2 (
    .D(adder_1_out), .Q(branchaddress_1_p3), .clk(registerfile_1_p2), .clr(Reset));  // open: en
  Register #(.width(32)) register_3 (
    .D(ram_1_data), .Q(register_3_q), .clk(registerfile_1_p2), .clr(Reset));  // open: en
  // InstructionDecode instructiondecode_1: pin names not known; wires that end beside it: register_3_q, instructiondecode_1_p2, instructiondecode_1_p3, instructiondecode_1_p4, instructiondecode_1_p5, instructiondecode_1_p6, instructiondecode_1_p7
  RAM #(.dataWidth(32)) ram_1 (
    .addr(wordaddress_1_p2), .data(ram_1_data), .sel(1'b1), .clk(1'b0), .ld(1'b1), .clr(Clear));
  and and_1 (and_1_out, brancheq_1_out_6, control_1_p3[0]);
  // Control control_1: pin names not known; wires that end beside it: instructiondecode_1_p2, control_1_p2, control_1_p3[0], control_1_p3[1], control_1_p3[2], control_1_p6, control_1_p3[5], control_1_p3[6], control_1_p3[7]
  Multiplexer #(.width(5), .enable("false")) multiplexer_2 (
    .in0(instructiondecode_1_p4), .in1(instructiondecode_1_p5), .out(multiplexer_2_out), .sel(control_1_p2));
  not not_1 (not_1_out, registerfile_1_p2);
  // SignExtend signextend_1: pin names not known; wires that end beside it: instructiondecode_1_p7, branchaddress_1_p2
  and and_2 (and_2_out, not_1_out, register_16_q[1]);
  // RegisterFile registerfile_1: pin names not known; wires that end beside it: registerfile_1_p1, registerfile_1_p2, register_16_q[1], registerfile_1_p4, instructiondecode_1_p3, instructiondecode_1_p4
  brancheq brancheq_1 (
    .in_1(instructiondecode_1_p3), .in_2(instructiondecode_1_p4), .in_3(registers_1_p7),
    .in_4(registers_1_p8), .out_6(brancheq_1_out_6));  // open: _0
  // Registers registers_1: pin names not known; wires that end beside it: instructiondecode_1_p3, instructiondecode_1_p4, registerfile_1_p4, registerfile_1_p1, and_2_out, Reset, registers_1_p7, registers_1_p8
  Register #(.width(32)) register_4 (
    .D(branchaddress_1_p3), .Q(register_4_q), .clk(registerfile_1_p2), .clr(Reset));  // open: en
  Register register_5 (
    .D({control_1_p3[7:5], control_1_p6, control_1_p3[2:0]}), .Q(register_5_q), .clk(registerfile_1_p2),
    .clr(Reset));  // open: en
  Register #(.width(32)) register_6 (
    .D(registers_1_p7), .Q(register_6_q), .clk(registerfile_1_p2), .clr(Reset));  // open: en
  Register #(.width(32)) register_7 (
    .D(registers_1_p8), .Q(register_7_q), .clk(registerfile_1_p2), .clr(Reset));  // open: en
  Register #(.width(5)) register_8 (
    .D(multiplexer_2_out), .Q(register_8_q), .clk(registerfile_1_p2), .clr(Reset));  // open: en
  Register #(.width(32)) register_9 (
    .D(branchaddress_1_p2), .Q(register_9_q), .clk(registerfile_1_p2), .clr(Reset));  // open: en
  Register #(.width(6)) register_10 (
    .D(instructiondecode_1_p6), .Q(register_10_q), .clk(registerfile_1_p2), .clr(Reset));  // open: en
  // BranchAddress branchaddress_2: pin names not known; wires that end beside it: register_4_q, register_9_q, branchaddress_2_p3, branchaddress_2_p4, branchaddress_2_p5
  Multiplexer #(.width(32), .enable("false")) multiplexer_3 (
    .in0(register_7_q), .in1(register_9_q), .out(multiplexer_3_out), .sel(register_5_q[6]));
  // ALUcontrol alucontrol_1: pin names not known; wires that end beside it: register_10_q, register_5_q[4:3], alucontrol_1_p3
  // ALU alu_1: pin names not known; wires that end beside it: register_6_q, multiplexer_3_out, alucontrol_1_p3, alu_1_p4[0], alu_1_p5
  Register #(.width(32)) register_11 (
    .D(branchaddress_2_p5), .Q(branchaddress_2_p4), .clk(registerfile_1_p2), .clr(Reset));  // open: en
  Register #(.width(6)) register_12 (
    .D({register_5_q[7], register_5_q[5], register_5_q[2:0], alu_1_p4[0]}), .Q(register_12_q),
    .clk(registerfile_1_p2), .clr(Reset));  // open: en
  Register #(.width(32)) register_13 (
    .D(alu_1_p5), .Q(register_13_q), .clk(registerfile_1_p2), .clr(Reset));  // open: en
  Register #(.width(32)) register_14 (
    .D(register_7_q), .Q(register_14_q), .clk(registerfile_1_p2), .clr(Reset));  // open: en
  Register #(.width(5)) register_15 (
    .D(register_8_q), .Q(register_15_q), .clk(registerfile_1_p2), .clr(Reset));  // open: en
  // MemoryData memorydata_1: pin names not known; wires that end beside it: register_12_q[5], register_14_q, memorydata_1_p3, register_12_q[4], register_12_q[2], memorydata_1_p6, memorydata_1_p3
  and and_3 (branchaddress_2_p3, register_12_q[0], register_12_q[1]);
  // WordAddress wordaddress_2: pin names not known; wires that end beside it: register_13_q, wordaddress_2_p2
  not not_2 (not_2_out, registerfile_1_p2);
  Register #(.width(2)) register_16 (
    .D({register_12_q[5], register_12_q[3]}), .Q(register_16_q), .clk(registerfile_1_p2), .clr(Reset));  // open: en
  Register #(.width(32)) register_17 (
    .D(register_13_q), .Q(register_17_q), .clk(registerfile_1_p2), .clr(Reset));  // open: en
  Register #(.width(32)) register_18 (
    .D(memorydata_1_p6), .Q(register_18_q), .clk(registerfile_1_p2), .clr(Reset));  // open: en
  Register #(.width(5)) register_19 (
    .D(register_15_q), .Q(registerfile_1_p4), .clk(registerfile_1_p2), .clr(Reset));  // open: en
  Clock Clock (.out(registerfile_1_p2));
  and and_4 (and_4_out, not_2_out, register_12_q[4]);
  RAM #(.dataWidth(32)) ram_2 (
    .addr(wordaddress_2_p2), .data(memorydata_1_p3), .sel(1'b1), .clk(and_4_out), .ld(register_12_q[2]),
    .clr(Clear_2));
  Multiplexer #(.width(32), .enable("false")) multiplexer_4 (
    .in0(register_17_q), .in1(register_18_q), .out(registerfile_1_p1), .sel(register_16_q[0]));
  not not_3 (not_3_out, 1'b0);
  Counter #(.ongoal("continue")) counter_1 (
    .load(1'b0), .count(not_3_out), .clk(registerfile_1_p2));  // open: D, Q, carry, clr

  // Notes on the sheet:
  //   Today's Date
  //   Your Name
  //   PC
  //   IF/ID
  //   Instruction Memory
  //   Decode
  //   IF/ID.rs
  //   IF/ID.rt
  //   IF/ID.rd
  //   Control
  //   Extend
  //   superBranch
  //   ID/EX
  //   Branch
  //   ALU
  //   ALU control
  //   EX/MEM
  //   regwrite
  //   MEM/WB
  //   Data Memory
endmodule

module Equality (
  input  [31:0] in_1,
  input  [31:0] in_2,
  output _0
);

  wire [31:0] xor_1_out;

  assign xor_1_out = in_1 ^ in_2;  // XOR_Gate xor_1, 32 bits wide
  // Zero zero_1: pin names not known; wires that end beside it: xor_1_out, _0
endmodule

module brancheq (
  input  [4:0] in_1,
  input  [4:0] in_2,
  input  [31:0] in_3,
  input  [31:0] in_4,
  output _0,
  output out_6
);

  wire equality_1__0;
  wire [31:0] xor_1_out;

  assign xor_1_out = {{27{1'b0}}, in_1} ^ {{27{1'b0}}, in_2};  // XOR_Gate xor_1, 32 bits wide
  // Zero zero_1: pin names not known; wires that end beside it: xor_1_out, _0
  Equality equality_1 (.in_1(in_3), .in_2(in_4), ._0(equality_1__0));
  or or_1 (out_6, _0, equality_1__0);
endmodule
