// Logisim project pipelineforwardingback.circ as structural Verilog: 3 circuits, main circuit Datapath
module Datapath (
  input  Reset,
  input  Clear,
  input  Clear_2
);

  wire alucontrol_1_p3, and_2_out, and_3_out, instructiondecode_1_p2, instructiondecode_1_p7, not_1_out,
       not_2_out, registers_1_p5;
  wire [0:0] alu_1_p4;
  wire [1:0] control_1_p6, register_18_q;
  wire [4:0] instructiondecode_1_p3, instructiondecode_1_p4, instructiondecode_1_p5, multiplexer_3_out,
       register_9_q, register_11_q, register_12_q, register_17_q, registers_1_p3;
  wire [5:0] instructiondecode_1_p6, register_10_q, register_14_q;
  wire [7:0] wordaddress_1_p2, wordaddress_2_p2;
  wire [8:0] control_1_p3, register_5_q;
  wire [31:0] adder_1_out, alu_1_p5, branchaddress_1_p3, memorydata_1_p4, memorydata_1_p7, multiplexer_1_out,
       multiplexer_2_out, ram_1_data, register_1_q, register_2_q, register_3_q, register_4_q, register_6_q,
       register_7_q, register_8_q, register_13_q, register_15_q, register_16_q, register_19_q, register_20_q,
       registers_1_p4, registers_1_p7, registers_1_p8, signextend_1_p2;

  Register #(.width(32)) register_1 (.D(multiplexer_1_out), .Q(register_1_q), .clk(Reset), .clr(Reset));  // open: en
  Multiplexer #(.width(32), .enable("false")) multiplexer_1 (
    .in0(adder_1_out), .in1(register_13_q), .out(multiplexer_1_out), .sel(and_2_out));
  // WordAddress wordaddress_1: pin names not known; wires that end beside it: register_1_q, wordaddress_1_p2
  Adder #(.width(32)) adder_1 (.a(32'h4), .b(register_1_q), .out(adder_1_out));  // open: cin, cout
  Register #(.width(32)) register_2 (.D(adder_1_out), .Q(register_2_q), .clk(Reset), .clr(Reset));  // open: en
  Register #(.width(32)) register_3 (.D(ram_1_data), .Q(register_3_q), .clk(Reset), .clr(Reset));  // open: en
  // InstructionDecode instructiondecode_1: pin names not known; wires that end beside it: register_3_q, instructiondecode_1_p2, instructiondecode_1_p3, instructiondecode_1_p4, instructiondecode_1_p5, instructiondecode_1_p6, instructiondecode_1_p7
  RAM #(.dataWidth(32)) ram_1 (
    .addr(wordaddress_1_p2), .data(ram_1_data), .sel(1'b1), .clk(1'b0), .ld(1'b1), .clr(Clear));
  // Control control_1: pin names not known; wires that end beside it: instructiondecode_1_p2, control_1_p3[8], control_1_p3[0], control_1_p3[1], control_1_p3[2], control_1_p6, control_1_p3[5], control_1_p3[6], control_1_p3[7]
  // Registers registers_1: pin names not known; wires that end beside it: instructiondecode_1_p3, instructiondecode_1_p4, registers_1_p3, registers_1_p4, registers_1_p5, Reset, registers_1_p7, registers_1_p8
  // SignExtend signextend_1: pin names not known; wires that end beside it: instructiondecode_1_p7, signextend_1_p2
  not not_1 (not_1_out, Reset);
  and and_1 (registers_1_p5, not_1_out, register_18_q[1]);
  Register #(.width(32)) register_4 (.D(register_2_q), .Q(register_4_q), .clk(Reset), .clr(Reset));  // open: en
  Register #(.width(9)) register_5 (
    .D({control_1_p3[8:5], control_1_p6, control_1_p3[2:0]}), .Q(register_5_q), .clk(Reset), .clr(Reset));  // open: en
  Register #(.width(32)) register_6 (.D(registers_1_p7), .Q(register_6_q), .clk(Reset), .clr(Reset));  // open: en
  Register #(.width(32)) register_7 (.D(registers_1_p8), .Q(register_7_q), .clk(Reset), .clr(Reset));  // open: en
  Register #(.width(32)) register_8 (.D(signextend_1_p2), .Q(register_8_q), .clk(Reset), .clr(Reset));  // open: en
  Register #(.width(5)) register_9 (
    .D(instructiondecode_1_p5), .Q(register_9_q), .clk(Reset), .clr(Reset));  // open: en
  Register #(.width(6)) register_10 (
    .D(instructiondecode_1_p6), .Q(register_10_q), .clk(Reset), .clr(Reset));  // open: en
  Register #(.width(5)) register_11 (
    .D(instructiondecode_1_p4), .Q(register_11_q), .clk(Reset), .clr(Reset));  // open: en
  Register #(.width(5)) register_12 (
    .D(instructiondecode_1_p3), .Q(register_12_q), .clk(Reset), .clr(Reset));  // open: en
  // BranchAddress branchaddress_1: pin names not known; wires that end beside it: register_4_q, register_8_q, branchaddress_1_p3
  Multiplexer #(.width(32), .enable("false")) multiplexer_2 (
    .in0(register_7_q), .in1(register_8_q), .out(multiplexer_2_out), .sel(register_5_q[6]));
  // ALUcontrol alucontrol_1: pin names not known; wires that end beside it: register_10_q, register_5_q[4:3], alucontrol_1_p3
  // ALU alu_1: pin names not known; wires that end beside it: register_6_q, multiplexer_2_out, alucontrol_1_p3, alu_1_p4[0], alu_1_p5
  Multiplexer #(.width(5), .enable("false")) multiplexer_3 (
    .in0(register_11_q), .in1(register_9_q), .out(multiplexer_3_out), .sel(register_5_q[8]));
  DataForwarding dataforwarding_1 ();  // open: ID_EX_rs, ForwardA, ID_EX_rt, ForwardB, EX_MEM_rd, Ex_MEM_RegWrite, MEM_WB_RegWrite, MEM_WB_rd
  Register #(.width(32)) register_13 (.D(branchaddress_1_p3), .Q(register_13_q), .clk(Reset), .clr(Reset));  // open: en
  Register #(.width(6)) register_14 (
    .D({register_5_q[7], register_5_q[5], register_5_q[2:0], alu_1_p4[0]}), .Q(register_14_q), .clk(Reset),
    .clr(Reset));  // open: en
  Register #(.width(32)) register_15 (.D(alu_1_p5), .Q(register_15_q), .clk(Reset), .clr(Reset));  // open: en
  Register #(.width(32)) register_16 (.D(register_7_q), .Q(register_16_q), .clk(Reset), .clr(Reset));  // open: en
  Register #(.width(5)) register_17 (.D(multiplexer_3_out), .Q(register_17_q), .clk(Reset), .clr(Reset));  // open: en
  // MemoryData memorydata_1: pin names not known; wires that end beside it: registers_1_p3, register_17_q, register_16_q, memorydata_1_p4, register_14_q[4], register_14_q[2], memorydata_1_p7, memorydata_1_p4
  and and_2 (and_2_out, register_14_q[0], register_14_q[1]);
  // WordAddress wordaddress_2: pin names not known; wires that end beside it: register_15_q, wordaddress_2_p2
  not not_2 (not_2_out, Reset);
  Register #(.width(2)) register_18 (
    .D({register_14_q[5], register_14_q[3]}), .Q(register_18_q), .clk(Reset), .clr(Reset));  // open: en
  Register #(.width(32)) register_19 (.D(register_15_q), .Q(register_19_q), .clk(Reset), .clr(Reset));  // open: en
  Register #(.width(32)) register_20 (.D(memorydata_1_p7), .Q(register_20_q), .clk(Reset), .clr(Reset));  // open: en
  Register #(.width(5)) register_21 (.D(register_17_q), .Q(registers_1_p3), .clk(Reset), .clr(Reset));  // open: en
  Clock Clock (.out(Reset));
  and and_3 (and_3_out, not_2_out, register_14_q[4]);
  RAM #(.dataWidth(32)) ram_2 (
    .addr(wordaddress_2_p2), .data(memorydata_1_p4), .sel(1'b1), .clk(and_3_out), .ld(register_14_q[2]),
    .clr(Clear_2));
  Multiplexer #(.width(32), .enable("false")) multiplexer_4 (
    .in0(register_19_q), .in1(register_20_q), .out(registers_1_p4), .sel(register_18_q[0]));

  // Notes on the sheet:
  //   Today's Date
  //   Your Name
  //   PC
  //   IF/ID
  //   Instruction Memory
  //   Decode
  //   IF/ID.rs
  //   IF/ID.rt
  //   IF/ID.rd
  //   Control
  //   Registers
  //   Extend
  //   IF/ID.rs
  //   IF/ID.rd
  //   IF/ID.rt
  //   ID/EX
  //   ID/EX.rd
  //   ID/EX.rt
  //   ID/EX.rs
  //   Branch
  //   ALU
  //   ALU control
  //   MEM\WB.regw
  //   EX\MEM.rd
  //   MEM\WB.rd
  //   EX\MEM.regw
  //   EX/MEM
  //   EX\MEM.rw
  //   MEM/WB
  //   Data Memory
endmodule

module Equality (
  input  [31:0] in_1,
  input  [31:0] in_2,
  output _0
);

  wire [31:0] zero_1_p1;

  // Zero zero_1: pin names not known; wires that end beside it: zero_1_p1, _0
  assign zero_1_p1 = in_1 ^ in_2;  // XOR_Gate xor_1, 32 bits wide
endmodule

module DataForwarding (
  input  [31:0] EX_MEM_rd,
  input  [31:0] ID_EX_rs,
  input  Ex_MEM_RegWrite,
  input  MEM_WB_RegWrite,
  input  [31:0] MEM_WB_rd,
  input  [31:0] ID_EX_rt,
  output [1:0] ForwardA,
  output [1:0] ForwardB
);

  wire and_3_out, and_4_out, and_5_out, equality_1__0, equality_2__0, equality_3__0, equality_4__0,
       equality_5__0, equality_6__0, not_1_out, not_2_out, not_3_out, not_4_out, not_5_out;

  and MEM_WB_ForwardA (ForwardA[0], not_1_out, and_5_out, not_4_out, not_3_out, equality_1__0);
  and MEM_WB_ForwardB (ForwardB[0], not_2_out, and_5_out, not_4_out, not_3_out, equality_2__0);
  not not_1 (not_1_out, equality_3__0);
  and and_1 (ForwardA[1], equality_3__0, and_3_out);
  Equality equality_1 (.in_1(MEM_WB_rd), .in_2(ID_EX_rs), ._0(equality_1__0));
  and and_2 (ForwardB[1], and_3_out, equality_4__0);
  not not_2 (not_2_out, equality_4__0);
  Equality equality_2 (.in_1(ID_EX_rt), .in_2(MEM_WB_rd), ._0(equality_2__0));
  and and_3 (and_3_out, not_5_out, and_4_out);
  Equality equality_3 (.in_1(EX_MEM_rd), .in_2(ID_EX_rs), ._0(equality_3__0));
  not not_3 (not_3_out, and_3_out);
  not not_4 (not_4_out, equality_6__0);
  Equality equality_4 (.in_1(ID_EX_rt), .in_2(EX_MEM_rd), ._0(equality_4__0));
  not not_5 (not_5_out, equality_5__0);
  Equality equality_5 (.in_1({32{1'b0}}), .in_2(EX_MEM_rd), ._0(equality_5__0));
  and and_4 (and_4_out, Ex_MEM_RegWrite, 1'b1);
  and and_5 (and_5_out, 1'b1, MEM_WB_RegWrite);
  Equality equality_6 (.in_1({32{1'b0}}), .in_2(MEM_WB_rd), ._0(equality_6__0));
endmodule
